// Digital circuit BC.dig as structural Verilog
module BC (
  input  [63:0] RD0,
  input  [63:0] RD1,
  input  [1:0] BRop,
  output PCbr
);

  wire BEQ_eq, BGE_gt, BLT_lt, BNE_eq, comparator_1_eq, not_1_out, or_1_out;

  Comparator #(.Bits(64)) BEQ (.a(RD0), .b(RD1), .eq(BEQ_eq));  // open: gt, lt
  Comparator #(.Bits(64)) BNE (.a(RD0), .b(RD1), .eq(BNE_eq));  // open: gt, lt
  Comparator #(.Bits(64)) BLT (.a(RD0), .b(RD1), .lt(BLT_lt));  // open: gt, eq
  Comparator #(.Bits(64)) BGE (.a(RD0), .b(RD1), .gt(BGE_gt));  // open: eq, lt
  Comparator #(.Bits(64)) comparator_1 (.a(RD0), .b(RD1), .eq(comparator_1_eq));  // open: gt, lt
  not not_1 (not_1_out, BNE_eq);
  or or_1 (or_1_out, BGE_gt, comparator_1_eq);
  Multiplexer #(.Selector_Bits(2)) multiplexer_1 (
    .sel(BRop), .in_0(BEQ_eq), .in_1(not_1_out), .in_2(BLT_lt), .in_3(or_1_out), .out(PCbr));
endmodule
