// Digital circuit INAME.dig as structural Verilog
module INAME (
  input  [4:0] INUM,
  output [7:0] _0,
  output [7:0] _1,
  output [7:0] _2,
  output [7:0] _3
);

  ROM #(.AddrBits(5), .Bits(32)) INAM (.A(INUM), .sel(1'b1), .D({_3, _2, _1, _0}));

  // Notes on the sheet:
  //   contents of INAM (hex, n*v repeats v):
  //   41444449,534c4c49,53524c49,41444452,4d554c5f,534c4c5f,53524c5f,414e445f,5355425f,
  //   4a414c5f,4a414c52,4245515f,424e455f,424c545f,4247455f,53445f5f,53575f5f,53425f5f,
  //   4c445f5f,4c575f5f,4c425f5f
endmodule
