// Digital circuit InstDecoder.dig as structural Verilog
module InstDecoder (
  input  [31:0] IW,
  output ALUSrcA,
  output [2:0] ALUOp,
  output RFW,
  output [2:0] ALUSrcB,
  output [1:0] PCsel,
  output [1:0] WDsel,
  output [1:0] BrOp,
  output LD,
  output ST,
  output [1:0] MSZ,
  output [4:0] INUM
);

  wire b_type_1_beq, bge_1_bge, blt_1_blt, bne_1_bne, i_type_1_addi, i_type_1_slli, i_type_1_srli,
       i_type_jalr_1_jalr, j_type_1_j, ld_type_1_lb, ld_type_1_ld, ld_type_1_lw, or_type_1_or, r_type_1_add,
       r_type_1_and, r_type_1_mul, r_type_1_sll, r_type_1_srl, r_type_1_sub, sd_type_1_sb, sd_type_1_sd,
       sd_type_1_sw;
  wire [4:0] INUM_num;

  i_type i_type_1 (
    .opcode(IW[6:0]), .funct3(IW[14:12]), .funct6(IW[31:26]), .addi(i_type_1_addi), .slli(i_type_1_slli),
    .srli(i_type_1_srli));
  r_type r_type_1 (
    .opcode(IW[6:0]), .funct3(IW[14:12]), .funct7(IW[31:25]), .add(r_type_1_add), .mul(r_type_1_mul),
    .sll(r_type_1_sll), .srl(r_type_1_srl), .\and (r_type_1_and), .sub(r_type_1_sub));
  j_type j_type_1 (.opcode(IW[6:0]), .j(j_type_1_j));
  i_type_jalr i_type_jalr_1 (.opcode(IW[6:0]), .funct3(IW[14:12]), .jalr(i_type_jalr_1_jalr));
  b_type b_type_1 (.opcode(IW[6:0]), .funct3(IW[14:12]), .beq(b_type_1_beq));
  bne bne_1 (.opcode(IW[6:0]), .funct3(IW[14:12]), .bne(bne_1_bne));
  blt blt_1 (.opcode(IW[6:0]), .funct3(IW[14:12]), .blt(blt_1_blt));
  bge bge_1 (.opcode(IW[6:0]), .funct3(IW[14:12]), .bge(bge_1_bge));
  sd_type sd_type_1 (.opcode(IW[6:0]), .funct3(IW[14:12]), .sd(sd_type_1_sd), .sw(sd_type_1_sw), .sb(sd_type_1_sb));
  ld_type ld_type_1 (.opcode(IW[6:0]), .funct3(IW[14:12]), .ld(ld_type_1_ld), .lw(ld_type_1_lw), .lb(ld_type_1_lb));
  or_type or_type_1 (.opcode(IW[6:0]), .funct3(IW[14:12]), .funct7(IW[31:25]), .\or (or_type_1_or));
  PriorityEncoder #(.Selector_Bits(5)) u_INUM (
    .in0(i_type_1_addi), .in1(i_type_1_slli), .in2(i_type_1_srli), .in3(r_type_1_add), .in4(r_type_1_mul),
    .in5(r_type_1_sll), .in6(r_type_1_srl), .in7(r_type_1_and), .in8(r_type_1_sub), .in9(j_type_1_j),
    .in10(i_type_jalr_1_jalr), .in11(b_type_1_beq), .in12(bne_1_bne), .in13(blt_1_blt), .in14(bge_1_bge),
    .in15(sd_type_1_sd), .in16(sd_type_1_sw), .in17(sd_type_1_sb), .in18(ld_type_1_ld), .in19(ld_type_1_lw),
    .in20(ld_type_1_lb), .in21(or_type_1_or), .in22(1'b0), .in23(1'b0), .in24(1'b0), .in25(1'b0),
    .in26(1'b0), .in27(1'b0), .in28(1'b0), .in29(1'b0), .in30(1'b0), .in31(1'b0), .num(INUM_num));  // open: any
  ROM #(.AddrBits(5), .Bits(23)) rom_1 (
    .A(INUM_num), .sel(1'b1), .D({RFW, ALUOp, ALUSrcA, ALUSrcB, PCsel, WDsel, ST, LD, MSZ, INUM, BrOp}));

  // Other names for the same wires on the sheet: opcode[6:0] = IW[6:0]; funct3[2:0] = IW[14:12];
  //   funct7[6:0] = IW[31:25]; funct6[5:0] = IW[31:26]

  // Notes on the sheet:
  //   contents of rom_1 (hex, n*v repeats v):
  //   408000,588004,608008,40000c,500010,580014,600018,68001c,480020,452824,40a828,5c02c,
  //   5c031,5c036,5c03b,2063c,206c0,20744,409248,4092cc,409350,700054
endmodule
