// Digital circuit alu.dig as structural Verilog
module alu (
  input  [63:0] A,
  input  [63:0] B,
  input  [2:0] ALUOp,
  output [63:0] R
);

  wire [63:0] add_1_s, and_1_out, barrelshifter_1_out, barrelshifter_2_out, mul_1_mul, or_1_out, sub_1_s;

  Add #(.Bits(64)) add_1 (.a(A), .b(B), .c_i(1'b0), .s(add_1_s));  // open: c_o
  Sub #(.Bits(64)) sub_1 (.a(A), .b(B), .c_i(1'b0), .s(sub_1_s));  // open: c_o
  Mul #(.Signed("true"), .Bits(32)) mul_1 (.a(A[31:0]), .b(B[31:0]), .mul(mul_1_mul));
  BarrelShifter #(.Bits(64)) barrelshifter_1 (.in(A), .shift(B[6:0]), .out(barrelshifter_1_out));
  BarrelShifter #(.Bits(64), .direction("right")) barrelshifter_2 (.in(A), .shift(B[6:0]), .out(barrelshifter_2_out));
  assign and_1_out = A & B;  // And and_1, 64 bits wide
  assign or_1_out = A | B;  // Or or_1, 64 bits wide
  Multiplexer #(.Selector_Bits(3), .Bits(64)) multiplexer_1 (
    .sel(ALUOp), .in_0(add_1_s), .in_1(sub_1_s), .in_2(mul_1_mul), .in_3(barrelshifter_1_out),
    .in_4(barrelshifter_2_out), .in_5(and_1_out), .in_6(or_1_out), .in_7({64{1'b0}}), .out(R));
endmodule
