// Digital circuit b-type.dig as structural Verilog
module b_type (
  input  [6:0] opcode,
  input  [2:0] funct3,
  output beq
);

  wire b_type_eq, beq_eq;

  Comparator #(.Bits(7)) b_type (.a(opcode), .b(7'b1100011), .eq(b_type_eq));  // open: gt, lt
  Comparator #(.Bits(3)) u_beq (.a(funct3), .b(3'b000), .eq(beq_eq));  // open: gt, lt
  and and_1 (beq, b_type_eq, beq_eq);
endmodule
