// Digital circuit bge.dig as structural Verilog
module bge (
  input  [6:0] opcode,
  input  [2:0] funct3,
  output bge
);

  wire b_type_eq, bge_eq;

  Comparator #(.Bits(7)) b_type (.a(opcode), .b(7'b1100011), .eq(b_type_eq));  // open: gt, lt
  Comparator #(.Bits(3)) u_bge (.a(funct3), .b(3'b101), .eq(bge_eq));  // open: gt, lt
  and and_1 (bge, b_type_eq, bge_eq);
endmodule
