// Digital circuit bne.dig as structural Verilog
module bne (
  input  [6:0] opcode,
  input  [2:0] funct3,
  output bne
);

  wire b_type_eq, bne_eq;

  Comparator #(.Bits(7)) b_type (.a(opcode), .b(7'b1100011), .eq(b_type_eq));  // open: gt, lt
  Comparator #(.Bits(3)) u_bne (.a(funct3), .b(3'b001), .eq(bne_eq));  // open: gt, lt
  and and_1 (bne, b_type_eq, bne_eq);
endmodule
