// Digital circuit data-mem.dig as structural Verilog
module data_mem (
  input  [63:0] ADDR,
  input  [63:0] DATA,
  input  str,
  input  ld,
  input  CLK,
  input  [31:0] IW,
  output [63:0] D
);

  wire [63:0] DataMem_d;

  RAMDualPort #(.AddrBits(8), .Bits(64)) DataMem (
    .A(ADDR[10:3]), .Din(DATA), .str(str), .C(CLK), .ld(ld), .D(DataMem_d));
  Multiplexer #(.Selector_Bits(2), .Bits(64)) multiplexer_1 (
    .sel(IW[13:12]), .in_0({64{1'b0}}), .in_1({64{1'b0}}), .in_2({64{1'b0}}), .in_3(DataMem_d), .out(D));
endmodule
