// Digital circuit i-type-jalr.dig as structural Verilog
module i_type_jalr (
  input  [6:0] opcode,
  input  [2:0] funct3,
  output jalr
);

  wire i_type_jalr_eq, jalr_eq;

  Comparator #(.Bits(7)) i_type_jalr (.a(opcode), .b(7'b1100111), .eq(i_type_jalr_eq));  // open: gt, lt
  Comparator #(.Bits(3)) u_jalr (.a(funct3), .b(3'b000), .eq(jalr_eq));  // open: gt, lt
  and and_1 (jalr, i_type_jalr_eq, jalr_eq);
endmodule
