// Digital circuit i-type.dig as structural Verilog
module i_type (
  input  [6:0] opcode,
  input  [2:0] funct3,
  input  [5:0] funct6,
  output addi,
  output slli,
  output srli
);

  wire add_eq, comparator_1_eq, i_type_eq, slli_eq, srli_eq;

  Comparator #(.Bits(7)) i_type (.a(opcode), .b(7'b0010011), .eq(i_type_eq));  // open: gt, lt
  Comparator #(.Bits(3)) add (.a(funct3), .b(3'b000), .eq(add_eq));  // open: gt, lt
  Comparator #(.Bits(6)) comparator_1 (.a(funct6), .b({6{1'b0}}), .eq(comparator_1_eq));  // open: gt, lt
  Comparator #(.Bits(3)) u_slli (.a(funct3), .b(3'b001), .eq(slli_eq));  // open: gt, lt
  Comparator #(.Bits(3)) u_srli (.a(funct3), .b(3'b101), .eq(srli_eq));  // open: gt, lt
  and and_1 (addi, i_type_eq, add_eq);
  and and_2 (slli, i_type_eq, comparator_1_eq, slli_eq);
  and and_3 (srli, i_type_eq, comparator_1_eq, srli_eq);
endmodule
