// Digital circuit j-type.dig as structural Verilog
module j_type (
  input  [6:0] opcode,
  output j
);

  Comparator #(.Bits(7)) j_type (.a(opcode), .b(7'b1101111), .eq(j));  // open: gt, lt
endmodule
