// Digital circuit lb-sb.dig as structural Verilog
module lb_sb (
  input  ld,
  input  [63:0] IW,
  output [63:0] out_3
);

  wire [31:0] multiplexer_1_out;
  wire [63:0] data_mem_1_p3;

  // data_mem data_mem_1: pin names not known; wires that end beside it: IW[9:3], ld, data_mem_1_p3
  Multiplexer #(.Bits(32)) multiplexer_1 (
    .sel(IW[2]), .in_0(data_mem_1_p3[31:0]), .in_1(data_mem_1_p3[63:32]), .out(multiplexer_1_out));
  BitExtender #(.inputBits(32), .outputBits(64)) bitextender_1 (.in(multiplexer_1_out), .out(out_3));
  // Pins of 32 and 64 bits meet at IW
  // Pins of 1 and 64 bits meet at out_3
endmodule
