// Digital circuit ld-type.dig as structural Verilog
module ld_type (
  input  [6:0] opcode,
  input  [2:0] funct3,
  output ld,
  output lw,
  output lb
);

  wire lb_eq, ld_2_eq, ld_eq, ld_type_eq;

  Comparator #(.Bits(7)) ld_type (.a(opcode), .b(7'b0000011), .eq(ld_type_eq));  // open: gt, lt
  Comparator #(.Bits(3)) u_ld (.a(funct3), .b(3'b011), .eq(ld_eq));  // open: gt, lt
  Comparator #(.Bits(3)) ld_2 (.a(funct3), .b(3'b010), .eq(ld_2_eq));  // open: gt, lt
  Comparator #(.Bits(3)) u_lb (.a(funct3), .b(3'b000), .eq(lb_eq));  // open: gt, lt
  and and_1 (ld, ld_type_eq, ld_eq);
  and and_2 (lw, ld_type_eq, ld_2_eq);
  and and_3 (lb, ld_type_eq, lb_eq);
endmodule
