// Digital circuit load.dig as structural Verilog
module load (
  input  [63:0] target,
  input  [63:0] Do,
  input  [1:0] MSZ,
  output [63:0] Dout
);

  wire [7:0] multiplexer_2_out;
  wire [31:0] multiplexer_1_out;

  Multiplexer #(.Bits(32)) multiplexer_1 (.sel(target[2]), .in_0(Do[31:0]), .in_1(Do[63:32]), .out(multiplexer_1_out));
  Multiplexer #(.Selector_Bits(3), .Bits(8)) multiplexer_2 (
    .sel(target[2:0]), .in_0(Do[7:0]), .in_1(Do[15:8]), .in_2(Do[23:16]), .in_3(Do[31:24]), .in_4(Do[39:32]),
    .in_5(Do[47:40]), .in_6(Do[55:48]), .in_7(Do[63:56]), .out(multiplexer_2_out));
  Multiplexer #(.Selector_Bits(2), .Bits(64)) multiplexer_3 (
    .sel(MSZ), .in_0(Do), .in_1({{32{1'b0}}, multiplexer_1_out}), .in_2({{56{1'b0}}, multiplexer_2_out}),
    .in_3({64{1'b0}}), .out(Dout));
endmodule
