// Digital circuit or-type.dig as structural Verilog
module or_type (
  input  [6:0] opcode,
  input  [2:0] funct3,
  input  [6:0] funct7,
  output \or 
);

  wire or_2_eq, or_eq, r_type_eq;

  Comparator #(.Bits(7)) r_type (.a(opcode), .b(7'b0110011), .eq(r_type_eq));  // open: gt, lt
  Comparator #(.Bits(3)) u_or (.a(funct3), .b(3'b110), .eq(or_eq));  // open: gt, lt
  Comparator #(.Bits(7)) or_2 (.a(funct7), .b({7{1'b0}}), .eq(or_2_eq));  // open: gt, lt
  and and_1 (\or , r_type_eq, or_eq, or_2_eq);
endmodule
