// Digital circuit program_counter.dig as structural Verilog
module program_counter (
  input  [63:0] D,
  input  CLK,
  input  EN,
  input  CLR,
  output [63:0] Q
);

  wire [63:0] multiplexer_1_out;

  Multiplexer #(.Bits(64)) multiplexer_1 (.sel(CLR), .in_0(D), .in_1({64{1'b0}}), .out(multiplexer_1_out));
  Register #(.Bits(64)) register_1 (.D(multiplexer_1_out), .C(CLK), .en(EN), .Q(Q));
endmodule
