// Digital circuit project05.dig as structural Verilog
module project05 (
  input  CLK,
  input  EN,
  input  CLR,
  input  [4:0] PROG,
  output [63:0] A0,
  output [63:0] A1,
  output [63:0] A2,
  output DONE,
  output [63:0] A3
);

  wire ALUSrcA, and_2_out, CLK_t, LD, PCbr, RFW, ST;
  wire [1:0] BrOp, MSZ, PCsel, WDsel;
  wire [2:0] ALUOp, ALUSrcB;
  wire [4:0] INUM, rd, rs1, rs2;
  wire [6:0] store_1_a;
  wire [7:0] iname_1__0, iname_1__1, iname_1__2, iname_1__3;
  wire [31:0] iw;
  wire [63:0] BTA, Dout, imm_I, immdecoder_1_imm_b, immdecoder_1_imm_j, immdecoder_1_imm_s,
       multiplexer_1_out, multiplexer_2_out, multiplexer_3_out, multiplexer_4_out, multiplexer_5_out, PC,
       PC_plus_4_s, ramdualport_1_d, RD1, register_file_1_rd0, store_1_din, x0, x1, x2, x3, x4, x5, x6, x7,
       x8, x9, x14, x15, x16, x17, x18, x19, x20, x21, x22, x23, x24, x25, x26, x27, x28, x29, x30, x31;

  Multiplexer #(.Bits(64)) multiplexer_1 (.sel(PCbr), .in_0(PC_plus_4_s), .in_1(BTA), .out(multiplexer_1_out));
  Multiplexer #(.Selector_Bits(2), .Bits(64)) multiplexer_2 (
    .sel(PCsel), .in_0(PC_plus_4_s), .in_1(BTA), .in_2(multiplexer_1_out), .in_3({64{1'b0}}),
    .out(multiplexer_2_out));
  and and_1 (CLK_t, CLK, ~DONE);  // And
  Comparator #(.Bits(32)) End (.a(iw), .b(32'hc0001073), .eq(DONE));  // open: gt, lt
  // Probe on PC
  // Probe on iw
  // Probe on rs1
  // Probe on rs2
  // Probe on rd
  // Probe on imm_I
  LED led_1 (.in(DONE));
  register register_1 (.D(multiplexer_2_out), .CLK(CLK_t), .CLR(CLR), .EN(EN), .Q(PC));
  Add #(.Bits(64)) PC_plus_4 (.a(PC), .b(64'h4), .c_i(1'b0), .s(PC_plus_4_s));  // open: c_o
  // Probe on x0
  // Probe on x1
  // Probe on x2
  // Probe on x3
  // Probe on x4
  // Probe on x5
  // Probe on x6
  // Probe on x7
  INAME iname_1 (.INUM(INUM), ._0(iname_1__0), ._1(iname_1__1), ._2(iname_1__2), ._3(iname_1__3));
  // inst_mem inst_mem_1: pin names not known; wires that end beside it: PROG, PC[10:2], iw
  // Probe on iname_1__3
  // Probe on x8
  // Probe on x9
  // Probe on A0
  // Probe on A1
  // Probe on A2
  // Probe on A3
  // Probe on x14
  // Probe on x15
  // Probe on iname_1__2
  // Probe on iname_1__1
  // Probe on iname_1__0
  InstDecoder instdecoder_1 (
    .IW(iw), .ALUSrcA(ALUSrcA), .ALUOp(ALUOp), .RFW(RFW), .ALUSrcB(ALUSrcB), .PCsel(PCsel), .WDsel(WDsel),
    .BrOp(BrOp), .LD(LD), .ST(ST), .MSZ(MSZ), .INUM(INUM));
  RegDecoder regdecoder_1 (.IW(iw), .RS1(rs1), .RS2(rs2), .RD(rd));
  ImmDecoder immdecoder_1 (
    .IW(iw), .imm_S(immdecoder_1_imm_s), .imm_I(imm_I), .imm_B(immdecoder_1_imm_b), .imm_J(immdecoder_1_imm_j));  // open: imm_U
  // Probe on x16
  // Probe on x17
  // Probe on x18
  // Probe on x19
  // Probe on x20
  // Probe on x21
  // Probe on x22
  // Probe on x23
  // Probe on x24
  // Probe on x25
  // Probe on x26
  // Probe on x27
  // Probe on x28
  // Probe on x29
  // Probe on x30
  // Probe on x31
  Multiplexer #(.Selector_Bits(2), .Bits(64)) multiplexer_3 (
    .sel(WDsel), .in_0(BTA), .in_1(PC_plus_4_s), .in_2(Dout), .in_3({64{1'b0}}), .out(multiplexer_3_out));
  and and_2 (and_2_out, RFW, EN);
  register_file register_file_1 (
    .ReadReg0(rs1), .ReadReg1(rs2), .WriteReg(rd), .WriteData(multiplexer_3_out), .WriteEn(and_2_out),
    .CLK(CLK_t), .CLR(CLR), .RD0(register_file_1_rd0), .RD1(RD1), .x0(x0), .x1(x1), .x2(x2), .x3(x3),
    .x4(x4), .x5(x5), .x6(x6), .x7(x7), .x8(x8), .x9(x9), .x10(A0), .x11(A1), .x12(A2), .x13(A3), .x14(x14),
    .x15(x15), .x16(x16), .x17(x17), .x18(x18), .x19(x19), .x20(x20), .x21(x21), .x22(x22), .x23(x23),
    .x24(x24), .x25(x25), .x26(x26), .x27(x27), .x28(x28), .x29(x29), .x30(x30), .x31(x31));
  // Probe on register_file_1_rd0
  LED u_pcbr (.in(PCbr));
  // Probe on RD1
  BC bc_1 (.RD0(register_file_1_rd0), .RD1(RD1), .BRop(BrOp), .PCbr(PCbr));
  store store_1 (.target(BTA), .MSZ(MSZ), .RD1(RD1), .D(ramdualport_1_d), .Din(store_1_din), .A(store_1_a));
  RAMDualPort #(.AddrBits(7), .Bits(64)) ramdualport_1 (
    .A(store_1_a), .Din(store_1_din), .str(ST), .C(CLK_t), .ld(LD), .D(ramdualport_1_d));
  load load_1 (.target(BTA), .Do(ramdualport_1_d), .MSZ(MSZ), .Dout(Dout));
  Multiplexer #(.Bits(64)) multiplexer_4 (
    .sel(ALUSrcA), .in_0(register_file_1_rd0), .in_1(PC), .out(multiplexer_4_out));
  Multiplexer #(.Selector_Bits(3), .Bits(64)) multiplexer_5 (
    .sel(ALUSrcB), .in_0(RD1), .in_1(imm_I), .in_2(immdecoder_1_imm_j), .in_3(immdecoder_1_imm_b),
    .in_4(immdecoder_1_imm_s), .in_5({64{1'b0}}), .in_6({64{1'b0}}), .in_7({64{1'b0}}),
    .out(multiplexer_5_out));
  alu alu_1 (.A(multiplexer_4_out), .B(multiplexer_5_out), .ALUOp(ALUOp), .R(BTA));

  // Other names for the same wires on the sheet: x10[63:0] = A0; x11[63:0] = A1; x12[63:0] = A2; x13[63:0] = A3
endmodule

/* Test case unit:
CLR EN CLK PROG A0 A1 A2 A3
1   0   0   x    x    x    x    x
0   0   0   x    x    x    x    x
while (!(DONE))
0   1   C   18    x    x    x    x
end while
0   1   0   18 1  3  3  0
*/
