// Digital circuit r-type.dig as structural Verilog
module r_type (
  input  [6:0] opcode,
  input  [2:0] funct3,
  input  [6:0] funct7,
  output add,
  output mul,
  output sll,
  output srl,
  output \and ,
  output sub
);

  wire add_2_eq, add_eq, AND_eq, comparator_1_eq, mul_eq, r_type_eq, sll_eq, srl_eq, SUB_eq;

  Comparator #(.Bits(7)) r_type (.a(opcode), .b(7'b0110011), .eq(r_type_eq));  // open: gt, lt
  Comparator #(.Bits(3)) u_add (.a(funct3), .b(3'b000), .eq(add_eq));  // open: gt, lt
  Comparator #(.Bits(7)) add_2 (.a(funct7), .b({7{1'b0}}), .eq(add_2_eq));  // open: gt, lt
  Comparator #(.Bits(7)) u_mul (.a(funct7), .b(7'b0000001), .eq(mul_eq));  // open: gt, lt
  Comparator #(.Bits(3)) u_sll (.a(funct3), .b(3'b001), .eq(sll_eq));  // open: gt, lt
  Comparator #(.Bits(3)) u_srl (.a(funct3), .b(3'b101), .eq(srl_eq));  // open: gt, lt
  Comparator #(.Bits(3)) u_AND (.a(funct3), .b(3'b111), .eq(AND_eq));  // open: gt, lt
  Comparator #(.Bits(3)) u_SUB (.a(funct3), .b(3'b000), .eq(SUB_eq));  // open: gt, lt
  Comparator #(.Bits(7)) comparator_1 (.a(funct7), .b(7'b0100000), .eq(comparator_1_eq));  // open: gt, lt
  and and_2 (add, r_type_eq, add_eq, add_2_eq);
  and and_3 (mul, r_type_eq, add_eq, mul_eq);
  and and_4 (sll, r_type_eq, add_2_eq, sll_eq);
  and and_5 (srl, r_type_eq, add_2_eq, srl_eq);
  and and_6 (\and , r_type_eq, add_2_eq, AND_eq);
  and and_7 (sub, r_type_eq, comparator_1_eq, SUB_eq);
endmodule
