// Digital circuit sd-type.dig as structural Verilog
module sd_type (
  input  [6:0] opcode,
  input  [2:0] funct3,
  output sd,
  output sw,
  output sb
);

  wire sb_eq, sd_eq, sd_type_eq, sw_eq;

  Comparator #(.Bits(7)) sd_type (.a(opcode), .b(7'b0100011), .eq(sd_type_eq));  // open: gt, lt
  Comparator #(.Bits(3)) u_sd (.a(funct3), .b(3'b011), .eq(sd_eq));  // open: gt, lt
  Comparator #(.Bits(3)) u_sw (.a(funct3), .b(3'b010), .eq(sw_eq));  // open: gt, lt
  Comparator #(.Bits(3)) u_sb (.a(funct3), .b(3'b000), .eq(sb_eq));  // open: gt, lt
  and and_1 (sd, sd_type_eq, sd_eq);
  and and_2 (sw, sd_type_eq, sw_eq);
  and and_3 (sb, sd_type_eq, sb_eq);
endmodule
