// Digital circuit store.dig as structural Verilog
module store (
  input  [63:0] target,
  input  [1:0] MSZ,
  input  [63:0] RD1,
  input  [63:0] D,
  output [63:0] Din,
  output [6:0] A
);

  wire [63:0] multiplexer_1_out, multiplexer_2_out;

  Multiplexer #(.Bits(64)) multiplexer_1 (
    .sel(target[2]), .in_0({D[63:32], RD1[31:0]}), .in_1({RD1[31:0], D[31:0]}), .out(multiplexer_1_out));
  Multiplexer #(.Selector_Bits(3), .Bits(64)) multiplexer_2 (
    .sel(target[2:0]), .in_0({D[63:8], RD1[7:0]}), .in_1({D[63:16], RD1[7:0], D[7:0]}),
    .in_2({D[63:24], RD1[7:0], D[15:0]}), .in_3({D[63:32], RD1[7:0], D[23:0]}),
    .in_4({D[63:40], RD1[7:0], D[31:0]}), .in_5({D[63:48], RD1[7:0], D[39:0]}),
    .in_6({D[63:56], RD1[7:0], D[47:0]}), .in_7({RD1[7:0], D[63:56], D[47:0]}), .out(multiplexer_2_out));
  Multiplexer #(.Selector_Bits(2), .Bits(64)) multiplexer_3 (
    .sel(MSZ), .in_0(multiplexer_1_out), .in_1(RD1), .in_2(multiplexer_2_out), .in_3({64{1'b0}}), .out(Din));

  assign A = target[9:3];

  // Other names for the same wires on the sheet: b0[7:0] = D[7:0]; w0[31:0] = D[31:0]; b1[7:0] = D[15:8];
  //   b2[7:0] = D[23:16]; b3[7:0] = D[31:24]; b4[7:0] = D[39:32]; w1[31:0] = D[63:32]; b5[7:0] = D[47:40];
  //   b6[7:0] = D[55:48]; b7[7:0] = D[63:56]; bn[7:0] = RD1[7:0]; wn[31:0] = RD1[31:0]
endmodule
